# Fritzing sketch led_fadding with esp32 (saved by Fritzing 0.9.3b)
circuit board: 8.56866cm x 5.45239cm

parts:
  U1 = LuaNode32 / ESP32 [part_number=ESP32S-PIN30]
  LED2 = LED - 5mm [color="Red (633nm)" package="5 mm [THT]"]
  R1 = Resistor [tolerance=±5% resistance=220 package=THT]

nets:
  N1: U1.GND, LED2.cathode
  N2: U1.D22, R1.Pin_1
  N3: LED2.anode, R1.Pin_0

custom parts:
  LuaNode32 / ESP32: New Image for LuaNode32 DOIT ESP32 DEVKIT V1. Base parts from LuaNode32 / ESP32 ESP32 based LuaNode32 by G.Noorlander DOIT Esp32 DevKit v1 (30 pins long, 11 pins width) by Werner Rothschopf (modified by vanepp Dec 2018)
